// Digital circuit 1x16ram.dig as structural Verilog
module _1x16ram (
  input  clk,
  input  RS2,
  input  RS1,
  input  WS,
  input  [15:0] WD_15_0,
  output [15:0] RD1_15_0,
  output [15:0] RD2_15_0
);

  _1x4ram _1x4ram_1 (
    .WD_3_0(WD_15_0[3:0]), .WS(WS), .RS1(RS1), .RS2(RS2), .clk(clk), .RD1_3_0(RD1_15_0[3:0]),
    .RD2_3_0(RD2_15_0[3:0]));
  _1x4ram _1x4ram_2 (
    .WD_3_0(WD_15_0[7:4]), .WS(WS), .RS1(RS1), .RS2(RS2), .clk(clk), .RD1_3_0(RD1_15_0[7:4]),
    .RD2_3_0(RD2_15_0[7:4]));
  _1x4ram _1x4ram_3 (
    .WD_3_0(WD_15_0[11:8]), .WS(WS), .RS1(RS1), .RS2(RS2), .clk(clk), .RD1_3_0(RD1_15_0[11:8]),
    .RD2_3_0(RD2_15_0[11:8]));
  _1x4ram _1x4ram_4 (
    .WD_3_0(WD_15_0[15:12]), .WS(WS), .RS1(RS1), .RS2(RS2), .clk(clk), .RD1_3_0(RD1_15_0[15:12]),
    .RD2_3_0(RD2_15_0[15:12]));
endmodule
