// Digital circuit 1x4ram.dig as structural Verilog
module _1x4ram (
  input  clk,
  input  RS2,
  input  RS1,
  input  WS,
  input  [3:0] WD_3_0,
  output [3:0] RD1_3_0,
  output [3:0] RD2_3_0
);

  _1x1ram _1x1ram_1 (.WD(WD_3_0[0]), .WS(WS), .RS1(RS1), .RS2(RS2), .clk(clk), .RD1(RD1_3_0[0]), .RD2(RD2_3_0[0]));
  _1x1ram _1x1ram_2 (.WD(WD_3_0[1]), .WS(WS), .RS1(RS1), .RS2(RS2), .clk(clk), .RD1(RD1_3_0[1]), .RD2(RD2_3_0[1]));
  _1x1ram _1x1ram_3 (.WD(WD_3_0[2]), .WS(WS), .RS1(RS1), .RS2(RS2), .clk(clk), .RD1(RD1_3_0[2]), .RD2(RD2_3_0[2]));
  _1x1ram _1x1ram_4 (.WD(WD_3_0[3]), .WS(WS), .RS1(RS1), .RS2(RS2), .clk(clk), .RD1(RD1_3_0[3]), .RD2(RD2_3_0[3]));
endmodule
