// Digital circuit 4BIT_FA.dig as structural Verilog
module _4BIT_FA (
  input  [3:0] A,
  input  [3:0] B,
  output [3:0] S,
  output Co
);

  wire _1bit_fa_2_co, _1bit_fa_3_co, _1bit_fa_4_co;

  _1BIT_FA _1bit_fa_1 (.X(B[3]), .Y(A[3]), .Ci(_1bit_fa_2_co), .S(S[3]), .Co(Co));
  _1BIT_FA _1bit_fa_2 (.X(B[2]), .Y(A[2]), .Ci(_1bit_fa_3_co), .S(S[2]), .Co(_1bit_fa_2_co));
  _1BIT_FA _1bit_fa_3 (.X(B[1]), .Y(A[1]), .Ci(_1bit_fa_4_co), .S(S[1]), .Co(_1bit_fa_3_co));
  _1BIT_FA _1bit_fa_4 (.X(B[0]), .Y(A[0]), .Ci(1'b0), .S(S[0]), .Co(_1bit_fa_4_co));
endmodule
