// Digital circuit 4BIT_SHL.dig as structural Verilog
module _4BIT_SHL (
  input  [3:0] A_3_0,
  input  [3:0] B_3_0,
  output [3:0] O_3_0
);

  Multiplexer #(.Selector_Bits(2)) multiplexer_1 (
    .sel(B_3_0[1:0]), .in_0(A_3_0[0]), .in_1(A_3_0[1]), .in_2(A_3_0[2]), .in_3(A_3_0[3]), .out(O_3_0[3]));
  Multiplexer #(.Selector_Bits(2)) multiplexer_2 (
    .sel(B_3_0[1:0]), .in_0(1'b0), .in_1(A_3_0[0]), .in_2(A_3_0[1]), .in_3(A_3_0[2]), .out(O_3_0[2]));
  Multiplexer #(.Selector_Bits(2)) multiplexer_3 (
    .sel(B_3_0[1:0]), .in_0(1'b0), .in_1(1'b0), .in_2(A_3_0[0]), .in_3(A_3_0[1]), .out(O_3_0[1]));
  Multiplexer #(.Selector_Bits(2)) multiplexer_4 (
    .sel(B_3_0[1:0]), .in_0(1'b0), .in_1(1'b0), .in_2(1'b0), .in_3(A_3_0[0]), .out(O_3_0[0]));
endmodule
