// Digital circuit 4bitCPU.dig as structural Verilog
module _4bitCPU (
  input  [3:0] RA2_3_0,
  input  [3:0] WR_3_0,
  input  [15:0] WRD_15_0,
  input  WE,
  input  CLK,
  input  PC_en,
  output [15:0] RD2_15_0,
  output [3:0] Jump_Address,
  output [3:0] R_3_0,
  output [1:0] R1_1_0,
  output [1:0] R2_1_0,
  output [3:0] Value_3_0,
  output [3:0] A_3_0,
  output [3:0] B_3_0,
  output [1:0] Op_1_0
);

  wire CPU_clock, Imm_sel, JMP_sel, REG_en, SF, ZF;
  wire [3:0] _4bitpc_adder_1_o_3_0, multiplexer_1_out, multiplexer_2_out, RA1;
  wire [5:0] x;
  wire [15:12] _9x16ram_1_rd1_15_0;

  and and_1 (CPU_clock, PC_en, CLK);
  Multiplexer #(.Bits(4)) multiplexer_1 (
    .sel(JMP_sel), .in_0(_4bitpc_adder_1_o_3_0), .in_1(Jump_Address), .out(multiplexer_1_out));
  _4bitProgramCounter _4bitprogramcounter_1 (.I_3_0(multiplexer_1_out), .CLK(CPU_clock), .O_3_0(RA1));
  _4bitPC_ADDER _4bitpc_adder_1 (.I_3_0(RA1), .O_3_0(_4bitpc_adder_1_o_3_0));
  _9x16ram _9x16ram_1 (
    .WRD__15_0(WRD_15_0), .WR_3_0(WR_3_0), .CLK(CLK), .WE(WE), .RA1_3_0(RA1), .RA2_3_0(RA2_3_0),
    .RD1_15_0({_9x16ram_1_rd1_15_0, Jump_Address, Value_3_0[1:0], x}), .RD2_15_0(RD2_15_0));
  CU cu_1 (
    .Opcode_3_0(_9x16ram_1_rd1_15_0), .SF(SF), .ZF(ZF), .Imm_Sel(Imm_sel), .REG_EN(REG_en), .Op_1_0(Op_1_0),
    .JMP_SEL(JMP_sel));
  _4bitregSetWith3regs _4bitregsetwith3regs_1 (
    .Wr_1_0(Jump_Address[3:2]), .CLk(CPU_clock), .RegEN(REG_en), .Wrd_3_0(R_3_0), .A_3_0(A_3_0),
    .B_3_0(B_3_0), .Ra_1_0(Jump_Address[3:2]), .Rb_1_0(Jump_Address[1:0]));
  ALU alu_1 (.A_3_0(A_3_0), .B_3_0(multiplexer_2_out), .R_3_0(R_3_0), .OP_1_0(Op_1_0), .SF(SF), .ZF(ZF));  // open: CF
  Multiplexer #(.Bits(4)) multiplexer_2 (
    .sel(Imm_sel), .in_0(B_3_0), .in_1({Jump_Address[1:0], Value_3_0[1:0]}), .out(multiplexer_2_out));

  assign R1_1_0 = Jump_Address[3:2];
  assign R2_1_0 = Jump_Address[1:0];
  assign Value_3_0[3:2] = Jump_Address[1:0];

  // Other names for the same wires on the sheet: xx[5:0] = x; val[3:0] = {Jump_Address[1:0], Value_3_0[1:0]};
  //   x[7:6] = Value_3_0[1:0]; JMP_address[3:0] = Jump_Address; R2[1:0] = Jump_Address[1:0];
  //   R1[1:0] = Jump_Address[3:2]; Op[1:0] = Op_1_0; RA2[3:0] = RA2_3_0; rd2[15:0] = RD2_15_0; WR[3:0] = WR_3_0;
  //   WRD[15:0] = WRD_15_0
endmodule
