// Digital circuit 4bitPC ADDER.dig as structural Verilog
module _4bitPC_ADDER (
  input  [3:0] I_3_0,
  output [3:0] O_3_0
);

  _4BIT_FA _4bit_fa_1 (.A(I_3_0), .B(4'b0001), .S(O_3_0));  // open: Co
endmodule
