// Digital circuit 4bitProgramCounter.dig as structural Verilog
module _4bitProgramCounter (
  input  [3:0] I_3_0,
  input  CLK,
  output [3:0] O_3_0
);

  _1bitReg _1bitreg_1 (.Dout(O_3_0[0]), .Din(I_3_0[0]), .Sel(1'b1), .Clock(CLK));
  _1bitReg _1bitreg_2 (.Dout(O_3_0[1]), .Din(I_3_0[1]), .Sel(1'b1), .Clock(CLK));
  _1bitReg _1bitreg_3 (.Dout(O_3_0[2]), .Din(I_3_0[2]), .Sel(1'b1), .Clock(CLK));
  _1bitReg _1bitreg_4 (.Dout(O_3_0[3]), .Din(I_3_0[3]), .Sel(1'b1), .Clock(CLK));

  // Other names for the same wires on the sheet: I0 = I_3_0[0]; I1 = I_3_0[1]; I2 = I_3_0[2]; I3 = I_3_0[3];
  //   O0 = O_3_0[0]; O1 = O_3_0[1]; O2 = O_3_0[2]; O3 = O_3_0[3]
endmodule
