// Digital circuit 4bitReg.dig as structural Verilog
module _4bitReg (
  input  [3:0] Din_3_0,
  input  Sel,
  input  Clk,
  output [3:0] Dout_3_0
);

  _1bitReg _1bitreg_1 (.Dout(Dout_3_0[0]), .Din(Din_3_0[0]), .Sel(Sel), .Clock(Clk));
  _1bitReg _1bitreg_2 (.Dout(Dout_3_0[1]), .Din(Din_3_0[1]), .Sel(Sel), .Clock(Clk));
  _1bitReg _1bitreg_3 (.Dout(Dout_3_0[2]), .Din(Din_3_0[2]), .Sel(Sel), .Clock(Clk));
  _1bitReg _1bitreg_4 (.Dout(Dout_3_0[3]), .Din(Din_3_0[3]), .Sel(Sel), .Clock(Clk));
endmodule
