// Digital circuit 4bitregSetWith3regs.dig as structural Verilog
module _4bitregSetWith3regs (
  input  [1:0] Wr_1_0,
  input  RegEN,
  input  CLk,
  input  [3:0] Wrd_3_0,
  input  [1:0] Ra_1_0,
  input  [1:0] Rb_1_0,
  output [3:0] A_3_0,
  output [3:0] B_3_0
);

  wire ra0, ra1, ra2, reg0, reg1, reg2;
  wire [3:0] Do0, Do1, Do2;

  and and_1 (reg0, ra0, RegEN);
  and and_2 (reg1, ra1, RegEN);
  and and_3 (reg2, ra2, RegEN);
  Decoder #(.Selector_Bits(2)) decoder_1 (.sel(Wr_1_0), .out_0(ra0), .out_1(ra1), .out_2(ra2));  // open: out_3
  _4bitReg _4bitreg_1 (.Din_3_0(Wrd_3_0), .Sel(reg0), .Clk(CLk), .Dout_3_0(Do0));
  _4bitReg _4bitreg_2 (.Din_3_0(Wrd_3_0), .Sel(reg1), .Clk(CLk), .Dout_3_0(Do1));
  _4bitReg _4bitreg_3 (.Din_3_0(Wrd_3_0), .Sel(reg2), .Clk(CLk), .Dout_3_0(Do2));
  Multiplexer #(.Selector_Bits(2), .Bits(4)) multiplexer_1 (
    .sel(Ra_1_0), .in_0(Do0), .in_1(Do1), .in_2(Do2), .in_3(Do2), .out(A_3_0));
  Multiplexer #(.Selector_Bits(2), .Bits(4)) multiplexer_2 (
    .sel(Rb_1_0), .in_0(Do0), .in_1(Do1), .in_2(Do2), .in_3(Do2), .out(B_3_0));

  // Other names for the same wires on the sheet: Ao[3:0] = A_3_0; Bo[3:0] = B_3_0; Ra[1:0] = Ra_1_0; Rb[1:0] = Rb_1_0;
  //   regenout = RegEN
endmodule
