// Digital circuit ALU.dig as structural Verilog
module ALU (
  input  [3:0] A_3_0,
  input  [3:0] B_3_0,
  input  [1:0] OP_1_0,
  output [3:0] R_3_0,
  output CF,
  output SF,
  output ZF
);

  wire [3:0] _4bit_fa_1_s, _4bit_shl_1_o_3_0, _4bit_xor_1_out_3_0;

  _4BIT_XOR _4bit_xor_1 (.A_3_0(A_3_0), .B_3_0(B_3_0), .Out_3_0(_4bit_xor_1_out_3_0));
  _4BIT_SHL _4bit_shl_1 (.A_3_0(A_3_0), .B_3_0(B_3_0), .O_3_0(_4bit_shl_1_o_3_0));
  _4BIT_FA _4bit_fa_1 (.A(A_3_0), .B(B_3_0), .S(_4bit_fa_1_s), .Co(CF));
  Multiplexer #(.Selector_Bits(2), .Bits(4)) multiplexer_1 (
    .sel(OP_1_0), .in_0(_4bit_xor_1_out_3_0), .in_1(_4bit_shl_1_o_3_0), .in_2(_4bit_fa_1_s), .in_3(4'b0000),
    .out(R_3_0));
  nor nor_1 (ZF, R_3_0[0], R_3_0[1], R_3_0[2], R_3_0[3]);

  assign SF = R_3_0[0];

  // Other names for the same wires on the sheet: A[3:0] = A_3_0; B[3:0] = B_3_0; OP[1:0] = OP_1_0
endmodule
